// Logisim project adjclock.circ as structural Verilog: 1 circuit, main circuit main
module main (
  input  in_1,
  input  in_2,
  input  in_3,
  input  in_4,
  input  in_5,
  input  in_6,
  output out_7
);

  wire and_1_out, clock_1_out, d_ff_1_q, d_ff_2_q, d_ff_3_q, d_ff_3_qn, d_ff_4_q, d_ff_4_qn, n74163_1_pin1,
       n74163_1_pin3, n74163_1_pin4, n74163_1_pin5, n74163_1_pin6, n74163_1_pin7, n74163_1_pin9,
       n74163_1_pin10, n74163_1_pin11, n74175_1_pin9, not_1_out, not_2_out;

  Clock clock_1 (.out(clock_1_out));
  not not_1 (not_1_out, d_ff_4_q);
  D_Flip_Flop d_ff_1 (.D(in_1), .clk(not_1_out), .Q(d_ff_1_q));  // open: Qn, preset, reset
  D_Flip_Flop d_ff_2 (.D(d_ff_1_q), .clk(not_1_out), .Q(d_ff_2_q));  // open: Qn, preset, reset
  and and_1 (and_1_out, d_ff_1_q, not_2_out);
  not not_2 (not_2_out, d_ff_2_q);
  _74163 u_74163_1 (
    .pin1(n74163_1_pin1), .pin2(clock_1_out), .pin3(n74163_1_pin3), .pin4(n74163_1_pin4),
    .pin5(n74163_1_pin5), .pin6(n74163_1_pin6), .pin7(n74163_1_pin7), .pin12(out_7), .pin11(n74163_1_pin11),
    .pin10(n74163_1_pin10), .pin9(n74163_1_pin9));  // open: pin15, pin14, pin13
  _74175 u_74175_1 (
    .pin1(in_4), .pin2(n74163_1_pin5), .pin4(in_5), .pin5(in_6), .pin15(n74163_1_pin3), .pin13(in_2),
    .pin12(in_3), .pin10(n74163_1_pin4), .pin9(n74175_1_pin9));  // open: pin3, pin6, pin7, pin14, pin11
  not not_3 (n74163_1_pin9, n74163_1_pin11);
  D_Flip_Flop d_ff_3 (.D(d_ff_3_qn), .clk(clock_1_out), .Q(d_ff_3_q), .Qn(d_ff_3_qn));  // open: preset, reset
  D_Flip_Flop d_ff_4 (.D(d_ff_4_qn), .clk(n74163_1_pin9), .Q(d_ff_4_q), .Qn(d_ff_4_qn));  // open: preset, reset
  and and_2 (n74175_1_pin9, and_1_out, d_ff_4_q);
  // NAND_Gate nand_1 has open pins: in1=d_ff_3_q, out=open
  // Digital_Oscilloscope #(.nState(24)) digital_oscilloscope_1: pin names not known; wires that end beside it: clock_1_out, d_ff_4_q, and_1_out, n74175_1_pin9
  // also tied to GND on the sheet: n74163_1_pin6
  // also tied to VCC on the sheet: {n74163_1_pin1, n74163_1_pin10, n74163_1_pin7}
endmodule
