// Logisim project vidcounter4.circ as structural Verilog: 1 circuit, main circuit main
module main (
  input  in_1,
  input  in_2,
  input  in_3,
  input  in_4,
  input  in_5,
  input  in_6,
  input  in_7,
  input  in_8,
  input  in_9,
  input  serin,
  input  in_11,
  input  in_12,
  input  in_13,
  input  in_14,
  output out_15
);

  wire and_1_out, and_2_out, and_3_out, and_4_out, and_5_out, and_6_out, and_7_out, and_8_out, and_9_out,
       and_10_out, and_11_out, and_12_out, and_13_out, and_14_out, and_15_out, and_16_out, and_17_out,
       button_1_out, button_2_out, clock_1_out, d_ff_2_q, d_ff_3_q, d_ff_4_q, d_ff_5_q, d_ff_6_q, d_ff_7_q,
       d_ff_8_q, d_ff_9_q, d_ff_10_q, d_ff_11_q, d_ff_12_q, digital_oscilloscope_1_p2, n74163_1_pin1,
       n74163_1_pin6, n74163_1_pin7, n74163_1_pin9, n74163_1_pin10, n74163_1_pin11, not_1_out, not_3_out,
       not_4_out, not_5_out, or_1_out, or_2_out, or_3_out, or_4_out, or_5_out, or_6_out, or_7_out, or_8_out,
       or_9_out, undriven, xor_1_out, xor_2_out;
  wire [7:0] counter_1_q;

  Counter counter_1 (.clr(undriven), .clk(not_1_out), .Q(counter_1_q));  // open: load, up, count, D, carry
  not not_1 (not_1_out, xor_1_out);
  Button button_1 (.out(button_1_out));
  Clock clock_1 (.out(clock_1_out));
  xor xor_1 (xor_1_out, button_1_out, clock_1_out);
  D_Flip_Flop d_ff_1 ();  // open: D, clk, Q, Qn, preset, reset
  and and_1 (and_1_out, counter_1_q[3], xor_1_out);
  Button button_2 (.out(button_2_out));
  xor xor_2 (xor_2_out, and_1_out, button_2_out);
  _74163 u_74163_1 (
    .pin1(n74163_1_pin1), .pin2(xor_2_out), .pin3(in_11), .pin4(in_12), .pin5(in_13), .pin6(n74163_1_pin6),
    .pin7(n74163_1_pin7), .pin12(out_15), .pin11(n74163_1_pin11), .pin10(n74163_1_pin10), .pin9(n74163_1_pin9));  // open: pin15, pin14, pin13
  D_Flip_Flop d_ff_2 (.D(in_14), .clk(out_15), .Q(d_ff_2_q));  // open: Qn, preset, reset
  Counter counter_2 (.clr(in_1), .clk(n74163_1_pin11));  // open: load, up, count, D, carry, Q
  not not_2 (n74163_1_pin9, n74163_1_pin11);
  D_Flip_Flop d_ff_3 (.D(n74163_1_pin11), .clk(not_3_out), .Q(d_ff_3_q));  // open: Qn, preset, reset
  not not_3 (not_3_out, xor_2_out);
  D_Flip_Flop d_ff_4 (.D(d_ff_2_q), .clk(d_ff_3_q), .Q(d_ff_4_q));  // open: Qn, preset, reset
  not not_4 (not_4_out, n74163_1_pin9);
  and and_2 (and_2_out, not_4_out, in_2);
  and and_3 (and_3_out, serin, not_5_out);
  or or_1 (or_1_out, and_2_out, and_3_out);
  D_Flip_Flop d_ff_5 (.D(or_1_out), .clk(not_3_out), .Q(d_ff_5_q));  // open: Qn, preset, reset
  D_Flip_Flop d_ff_6 (.D(or_2_out), .clk(not_3_out), .Q(d_ff_6_q));  // open: Qn, preset, reset
  or or_2 (or_2_out, digital_oscilloscope_1_p2, d_ff_4_q);
  not not_5 (not_5_out, not_4_out);
  and and_4 (and_4_out, not_4_out, in_3);
  and and_5 (and_5_out, d_ff_5_q, not_5_out);
  or or_3 (or_3_out, and_4_out, and_5_out);
  D_Flip_Flop d_ff_7 (.D(or_3_out), .clk(not_3_out), .Q(d_ff_7_q));  // open: Qn, preset, reset
  and and_6 (and_6_out, not_4_out, in_4);
  or or_4 (or_4_out, and_6_out, and_8_out);
  D_Flip_Flop d_ff_8 (.D(or_4_out), .clk(not_3_out), .Q(d_ff_8_q));  // open: Qn, preset, reset
  and and_7 (and_7_out, not_4_out, in_5);
  and and_8 (and_8_out, d_ff_7_q, not_5_out);
  // Digital_Oscilloscope #(.nState(24)) digital_oscilloscope_1: pin names not known; wires that end beside it: xor_2_out, digital_oscilloscope_1_p2, d_ff_4_q, d_ff_6_q, d_ff_3_q, n74163_1_pin11, out_15, n74163_1_pin9
  and and_9 (and_9_out, d_ff_8_q, not_5_out);
  or or_5 (or_5_out, and_7_out, and_9_out);
  D_Flip_Flop d_ff_9 (.D(or_5_out), .clk(not_3_out), .Q(d_ff_9_q));  // open: Qn, preset, reset
  and and_10 (and_10_out, not_4_out, in_6);
  and and_11 (and_11_out, d_ff_9_q, not_5_out);
  or or_6 (or_6_out, and_10_out, and_11_out);
  D_Flip_Flop d_ff_10 (.D(or_6_out), .clk(not_3_out), .Q(d_ff_10_q));  // open: Qn, preset, reset
  and and_12 (and_12_out, not_4_out, in_7);
  and and_13 (and_13_out, d_ff_10_q, not_5_out);
  or or_7 (or_7_out, and_12_out, and_13_out);
  D_Flip_Flop d_ff_11 (.D(or_7_out), .clk(not_3_out), .Q(d_ff_11_q));  // open: Qn, preset, reset
  and and_14 (and_14_out, not_4_out, in_8);
  or or_8 (or_8_out, and_14_out, and_16_out);
  D_Flip_Flop d_ff_12 (.D(or_8_out), .clk(not_3_out), .Q(d_ff_12_q));  // open: Qn, preset, reset
  and and_15 (and_15_out, not_4_out, in_9);
  and and_16 (and_16_out, d_ff_11_q, not_5_out);
  and and_17 (and_17_out, d_ff_12_q, not_5_out);
  or or_9 (or_9_out, and_15_out, and_17_out);
  D_Flip_Flop d_ff_13 (.D(or_9_out), .clk(not_3_out), .Q(digital_oscilloscope_1_p2));  // open: Qn, preset, reset
  // also tied to GND on the sheet: n74163_1_pin6
  // also tied to VCC on the sheet: {n74163_1_pin1, n74163_1_pin10, n74163_1_pin7}

  // Notes on the sheet:
  //   load
  //   clk
  //   delay
  //   0
  //   1
  //   2
  //   3
  //   4
  //   5
  //   7
  //   6
endmodule
